# Fritzing sketch exercise_work_2 (saved by Fritzing 0.9.3b)
breadboards: 1

parts:
  Part1 = Arduino Uno (Rev3)
  Part2 = Arduino Mega 2560 (Rev3)
  LCD1 = LCD screen
  R1 = Trimmer Potentiometer [maximum_resistance=10kΩ package=THT]
  Part3 = HC-SR501 Body Sensor Module
  Keypad4x1 = Keypad Membran 4x4
  J2 = Piezo Speaker

nets:
  N1: Part1.A4/SDA, Part2.D20/SDA, Part2.SDA
  N2: Part1.A5/SCL, Part2.D21/SCL, Part2.SCL
  N3: Part1.D8, LCD1.DB7
  N4: Part1.D2, LCD1.RS
  N5: Part1.D3_PWM, LCD1.E
  N6: Part1.D5_PWM, LCD1.DB4
  N7: Part1.D6_PWM, LCD1.DB5
  N8: Part1.D7, LCD1.DB6
  GND: Part1.GND, Part2.GND, LCD1.VSS, LCD1.R/W, LCD1.LED-, R1.leg1, Part3.GND, J2.pin1
  N9: Part2.D11_PWM, J2.pin2
  N10: Part2.D10_PWM, Part3.OUT
  N11: Part2.D9_PWM, Keypad4x1.Pin8
  N12: Part2.D8_PWM, Keypad4x1.Pin7
  5V: Part2.5V, LCD1.VDD, LCD1.LED+, R1.leg2, Part3.VCC
  N13: Part2.D2_PWM, Keypad4x1.Pin1
  N14: Part2.D3_PWM, Keypad4x1.Pin2
  N15: Part2.D4_PWM, Keypad4x1.Pin3
  N16: Part2.D5_PWM, Keypad4x1.Pin4
  N17: Part2.D6_PWM, Keypad4x1.Pin5
  N18: Part2.D7_PWM, Keypad4x1.Pin6
  N19: LCD1.V0, R1.wiper

custom parts:
  HC-SR501 Body Sensor Module: Pyroelectric Infrared PIR Motion Sensor Detector Module
  Keypad Membran 4x4: Membrane Keypad 4x4 Matrix
